# Fritzing sketch led2_r-pi (saved by Fritzing 0.9.3b)
breadboards: 1

parts:
  Raspberry_Pi_1 = Raspberry Pi 3 [part_number=RPI-3-V1.2]
  LED1 = smd LED [color="Red (633nm)" package="0603 [SMD]"]
  R1 = Resistor [tolerance=±5% resistance=220 package=THT]
  LED2 = smd LED [color="Green (560nm)" package="0603 [SMD]"]
  R2 = Resistor [tolerance=±5% resistance=220 package=THT]

nets:
  N1: Raspberry_Pi_1.GPIO3, Raspberry_Pi_1.GND, R2.Pin_1
  N2: Raspberry_Pi_1.GIPO17, LED1.anode
  N3: Raspberry_Pi_1.GIPO5, LED2.anode
  N4: LED1.cathode, R1.Pin_0
  N5: LED2.cathode, R2.Pin_0
